// Logisim project Half Adder.circ as structural Verilog: 1 circuit, main circuit main
module main (
  input  in_1,
  input  in_2,
  output out_3,
  output out_4
);

  buf and_1 (out_4, in_2);  // AND_Gate
  // XOR_Gate xor_1 has open pins: out=out_3
endmodule
